# Fritzing sketch PCB-Scheme (saved by Fritzing 0.9.6b)
circuit board: 8cm x 6.5cm
circuit board: 8cm x 6.5cm
breadboards: 1

parts:
  J2 = Screw terminal - 2 pins [package=THT]
  Switch = SPST Switch [package=switch-spst-smd-a]
  PowerUnit = RioRand LM2596
  J9 = Screw terminal - 2 pins [package=THT]
  J10 = female pin header, 2 pins [form="♀ (female)"]
  Arduino_Micro1 = Arduino Micro (Rev3)
  LLC2 = Logic Level Converter [package="Breakout board"]
  J12 = Screw terminal - 2 pins [package=THT]
  J13 = female pin header, 6 pins [form="♀ (female)"]
  MPU6051 = InvenSense MPU6050
  Sonar1 = female pin header, 4 pins [form="♀ (female)"]
  PING1 = smd LED [color="Red (633nm)" package="0603 [SMD]"]
  Command = female pin header, 2 pins [form="♀ (female)"]
  R4 = Resistor [tolerance=±5% resistance=220 package="0402 [SMD]"]
  R5 = Resistor [tolerance=±5% resistance=220 package="0402 [SMD]"]
  Q2 = Basic FET P-Channel [package="TO220 [THT]"]
  J15 = female pin header, 2 pins [form="♀ (female)"]
  MCU2 = Raspberry Pi Zero
  J17 = Screw terminal - 2 pins [package=THT]
  Input = female pin header, 8 pins [form="♀ (female)"]  # not connected

nets:
  N1: J2.pin1, Switch.S, J17.pin1
  N2: J2.pin2, PowerUnit.Pin_2, J17.pin2
  N3: Switch.O, PowerUnit.Pin_1
  N4: PowerUnit.Pin_3, J9.pin1
  N5: PowerUnit.Pin_4, J9.pin2
  N6: J10.pin1, Q2.drain
  N7: Arduino_Micro1.D1/TX, LLC2.HV3
  N8: Arduino_Micro1.D0/RX, LLC2.HV4
  GND: Arduino_Micro1.GND, LLC2.L-GND, LLC2.H-GND, J12.pin2, MPU6051.GND, Sonar1.pin4, PING1.cathode, PING1.anode, Command.pin1, Command.pin2, R4.Pin_1, R5.Pin_1, Q2.source, MCU2.pin_6, MCU2.pin_9, MCU2.pin_14, MCU2.pin_25, MCU2.pin_34
  N9: Arduino_Micro1.D2/SDA, MPU6051.SDA, J15.pin2
  N10: Arduino_Micro1.D3/SCL, MPU6051.SCL, J15.pin1
  N11: Arduino_Micro1.D4_PWM/A6, J13.pin6
  N12: Arduino_Micro1.D5_PWM, J13.pin5
  N13: Arduino_Micro1.D6_PWM/A7, J13.pin4
  N14: Arduino_Micro1.D7, J13.pin3
  N15: Arduino_Micro1.D8_PWM/A8, J13.pin2
  N16: Arduino_Micro1.D12_PWM/A11, J13.pin1
  VIN: Arduino_Micro1.VIN, LLC2.HV, J12.pin1, MPU6051.VCC, Sonar1.pin3, MCU2.pin_2, MCU2.pin_4
  N17: Arduino_Micro1.A5, Sonar1.pin1
  N18: Arduino_Micro1.A4, Sonar1.pin2
  N19: Arduino_Micro1.A3, R4.Pin_0
  N20: Arduino_Micro1.A2, R5.Pin_0
  N21: Arduino_Micro1.D13_PWM, Q2.gate
  N22: LLC2.LV, MCU2.pin_1, MCU2.pin_17
  N23: LLC2.LV3, MCU2.pin_10

custom parts:
  Logic Level Converter: 5V to/from 3.3V logic level converter
