# Fritzing sketch scheme (saved by Fritzing 0.9.3b)
circuit board: 15.4267cm x 7.35182cm
breadboards: 1

parts:
  Lm2596 = RioRand LM2596
  Arduino = Arduino Micro (Rev3)
  CameraX = Dagu DGServo 9g header connector (female) [package=THT]
  CameraY = Dagu DGServo 9g header connector (female) [package=THT]
  Buzzer = Microphone  # not connected
  Ultrasonic = HY-SRF05 Ultrasonic Rangefinder
  S1 = Toggle Switch [package=THT]
  Power = Power plug

nets:
  GND: Lm2596.Pin_0, Arduino.GND, CameraX.pulse, CameraY.pulse, Ultrasonic.GND
  N1: Lm2596.Pin_1, Power.GND
  VCC: Lm2596.Pin_2, Arduino.5V, CameraX.Vcc, CameraY.Vcc
  N2: Lm2596.Pin_3, S1.L1
  N3: Arduino.D10_PWM/A10, CameraX.gnd
  N4: Arduino.D11_PWM, Ultrasonic.Echo
  N5: Arduino.D12_PWM/A11, Ultrasonic.Vcc
  N6: S1.L2, Power.VCC
